// Logisim project project.circ as structural Verilog: 3 circuits, main circuit main
module main (
  input  [2:0] M_S1_S0,
  input  Cin,
  input  A0,
  input  A1,
  input  A2,
  input  A3,
  input  B0,
  input  B1,
  input  B2,
  input  B3
);

  wire adder_1_cout, adder_2_cout, and_5_out, and_6_out, and_7_out, and_8_out, and_9_out, and_10_out,
       and_11_out, and_12_out, multiplexer_1_out, multiplexer_2_out, multiplexer_3_out, multiplexer_4_out,
       nor_1_out, nor_2_out, nor_3_out, nor_4_out, not_1_out, not_2_out, not_3_out, not_4_out, not_5_out,
       not_6_out, or_1_out, or_2_out, or_3_out, or_4_out, xor_5_out, xor_6_out, xor_7_out, xor_8_out,
       xor_9_out, xor_10_out, xor_11_out, xor_12_out, xor_13_out, xor_14_out;
  wire [3:0] adder_1_out, adder_2_out, and_1_out, xnor_1_out, xor_1_out;

  and and_1 (and_1_out[0], M_S1_S0[0], B0);
  and and_2 (and_1_out[1], M_S1_S0[0], B1);
  and and_3 (and_1_out[2], M_S1_S0[0], B2);
  and and_4 (and_1_out[3], M_S1_S0[0], B3);
  xor xor_1 (xor_1_out[0], M_S1_S0[0], A0);
  xor xor_2 (xor_1_out[1], M_S1_S0[0], A1);
  xor xor_3 (xor_1_out[2], M_S1_S0[0], A2);
  xor xor_4 (xor_1_out[3], M_S1_S0[0], A3);
  xnor xnor_1 (xnor_1_out[0], M_S1_S0[0], B0);
  xnor xnor_2 (xnor_1_out[1], M_S1_S0[0], B1);
  xnor xnor_3 (xnor_1_out[2], M_S1_S0[0], B2);
  xnor xnor_4 (xnor_1_out[3], M_S1_S0[0], B3);
  and and_5 (and_5_out, A0, B0);
  and and_6 (and_6_out, A1, B1);
  and and_7 (and_7_out, A2, B2);
  and and_8 (and_8_out, A3, B3);
  or or_1 (or_1_out, A0, B0);
  or or_2 (or_2_out, A1, B1);
  or or_3 (or_3_out, A2, B2);
  or or_4 (or_4_out, A3, B3);
  xor xor_5 (xor_5_out, A0, B0);
  xor xor_6 (xor_6_out, A1, B1);
  xor xor_7 (xor_7_out, A2, B2);
  xor xor_8 (xor_8_out, A3, B3);
  Adder #(.width(4)) adder_1 (.a({A3, A2, A1, A0}), .b(and_1_out), .out(adder_1_out), .cin(Cin), .cout(adder_1_cout));
  Adder #(.width(4)) adder_2 (.a(xor_1_out), .b(xnor_1_out), .out(adder_2_out), .cin(Cin), .cout(adder_2_cout));
  xor xor_9 (xor_9_out, A3, and_1_out[3]);
  xor xor_10 (xor_10_out, adder_1_out[3], adder_1_cout);
  xor xor_11 (xor_11_out, xor_1_out[3], xnor_1_out[3]);
  xor xor_12 (xor_12_out, adder_2_out[3], adder_2_cout);
  xor xor_13 (xor_13_out, xor_9_out, xor_10_out);
  xor xor_14 (xor_14_out, xor_11_out, xor_12_out);
  not not_1 (not_1_out, M_S1_S0[1]);
  and and_9 (and_9_out, xor_13_out, not_1_out);
  and and_10 (and_10_out, adder_1_cout, not_1_out);
  and and_11 (and_11_out, M_S1_S0[1], xor_14_out);
  and and_12 (and_12_out, adder_2_cout, M_S1_S0[1]);
  not not_2 (not_2_out, M_S1_S0[2]);
  nor nor_1 (nor_1_out, and_9_out, and_11_out);
  nor nor_2 (nor_2_out, and_10_out, and_12_out);
  nor nor_3 (nor_3_out, nor_1_out, not_2_out);
  nor nor_4 (nor_4_out, not_2_out, nor_2_out);
  LED V (.in(nor_3_out));
  LED Co (.in(nor_4_out));
  not not_3 (not_3_out, xor_6_out);
  not not_4 (not_4_out, xor_7_out);
  not not_5 (not_5_out, xor_5_out);
  Multiplexer #(.select(3), .enable("false")) multiplexer_1 (
    .in0(and_5_out), .in1(or_1_out), .in2(xor_5_out), .in3(not_5_out), .in4(adder_1_out[0]),
    .in5(adder_1_out[0]), .in6(adder_2_out[0]), .in7(adder_2_out[0]), .out(multiplexer_1_out), .sel(M_S1_S0));
  LED F0 (.in(multiplexer_1_out));
  Multiplexer #(.select(3), .enable("false")) multiplexer_2 (
    .in0(and_6_out), .in1(or_2_out), .in2(xor_6_out), .in3(not_3_out), .in4(adder_1_out[1]),
    .in5(adder_1_out[1]), .in6(adder_2_out[1]), .in7(adder_2_out[1]), .out(multiplexer_2_out), .sel(M_S1_S0));
  LED F2 (.in(multiplexer_3_out));
  Multiplexer #(.select(3), .enable("false")) multiplexer_3 (
    .in0(and_7_out), .in1(or_3_out), .in2(xor_7_out), .in3(not_4_out), .in4(adder_1_out[2]),
    .in5(adder_1_out[2]), .in6(adder_2_out[2]), .in7(adder_2_out[2]), .out(multiplexer_3_out), .sel(M_S1_S0));
  not not_6 (not_6_out, xor_8_out);
  LED F3 (.in(multiplexer_4_out));
  Multiplexer #(.select(3), .enable("false")) multiplexer_4 (
    .in0(and_8_out), .in1(or_4_out), .in2(xor_8_out), .in3(not_6_out), .in4(adder_1_out[3]),
    .in5(adder_1_out[3]), .in6(adder_2_out[3]), .in7(adder_2_out[3]), .out(multiplexer_4_out), .sel(M_S1_S0));
  LED F1 (.in(multiplexer_2_out));
endmodule

module aa (
  input  A,
  input  B,
  input  S1,
  input  S2,
  output Ao,
  output Bo
);

  wire and_1_out, and_2_out, and_3_out, and_4_out, and_5_out, not_1_out, not_2_out, not_3_out, not_4_out,
       not_5_out;

  not not_1 (not_1_out, A);
  and and_1 (and_1_out, not_1_out, S1, S2);
  and and_2 (and_2_out, A, not_2_out);
  not not_2 (not_2_out, S1);
  and and_3 (and_3_out, A, not_3_out);
  not not_3 (not_3_out, S2);
  not not_4 (not_4_out, B);
  and and_4 (and_4_out, not_4_out, S1, not_5_out);
  not not_5 (not_5_out, S2);
  and and_5 (and_5_out, B, S2);
  or or_1 (Ao, and_1_out, and_2_out, and_3_out);
  or or_2 (Bo, and_4_out, and_5_out);
endmodule

module mm (
  input  A,
  input  B,
  input  S1,
  input  S2,
  output Ao,
  output Bo
);

  wire not_1_out, not_2_out, not_3_out, or_1_out, or_2_out, or_3_out;

  or or_1 (or_1_out, A, S1);
  or or_2 (or_2_out, A, S2);
  not not_1 (not_1_out, A);
  not not_2 (not_2_out, S1);
  or or_3 (or_3_out, not_1_out, not_2_out, not_3_out);
  not not_3 (not_3_out, S2);
  xnor xnor_1 (Bo, B, S2);
  and and_1 (Ao, or_1_out, or_2_out, or_3_out);
endmodule
